# Fritzing sketch Car (saved by Fritzing 0.9.1b)
breadboards: 1

parts:
  Parte1 = Arduino Uno (Rev3) - ICSP
  M1 = DC Motor
  IC1 = L293D [package=THT]
  U1 = DIODE-ZENER [package=diode-zener]  # not connected
  U2 = DIODE-ZENER [package=diode-zener]
  U3 = DIODE-ZENER [package=diode-zener]
  U4 = DIODE-ZENER [package=diode-zener]
  J1 = Piezo Speaker
  R1 = Resistor [tolerance=±5% resistance=1k package="0805 [SMD]"]

nets:
  N1: Parte1.D3_PWM, J1.pin2
  N2: Parte1.D5_PWM, IC1.In_2
  N3: Parte1.D6_PWM, IC1.In_1
  N4: Parte1.GND, IC1.0V, R1.Pin_1
  N5: Parte1.VIN, IC1.Enable_1, IC1.+Vmotor, IC1.+V, U4.C
  N6: M1.pin_1, IC1.Out_2_(_Controlled_by_Enable_1_), U2.C
  N7: M1.pin_2, IC1.Out_1_(_Controlled_by_Enable_1_), U3.C
  N8: J1.pin1, R1.Pin_0

notes:
  Back wheels
  Claxon
